# Fritzing sketch SmartGarden (saved by Fritzing 0.9.3b)
breadboards: 1

parts:
  Part1 = Arduino Pro Mini (3.3V)
  U2 = ESP8266 ESP-01 Upgraded WiFi Module [part_number=ESP8266]
  VCC1 = Battery
  M1 = HTU21d
  Part2 = FC-28 Soil Hygrometer Module - Probe
  Part3 = FC-28 Soil Hygrometer Module
  U3 = Mini-360 DC-DC Buck converter [package=THT]
  WATER_PUMP1 = water pump/motor  # not connected
  Part4 = IFR520 MOS module [package=THT]
  VCC2 = 4 x AAA Battery Mount
  R1 = Resistor [tolerance=±5% resistance=1k package=THT]
  R2 = Resistor [tolerance=±5% resistance=2k package=THT]

nets:
  GND: Part1.DTR, VCC1.-, M1.GND, Part3.GND, U3.IN-, Part4.GND, VCC2.-, R2.Pin_1
  N1: Part1.A4, M1.SDA
  N2: Part1.A5, M1.SCL
  VCC: Part1.RAW, Part4.VCC, Part4.VIN, VCC2.+
  N3: Part1.A0, Part3.AO
  N4: Part1.D4, Part4.SIG
  N5: Part1.RXI, U2.TXD
  N6: Part1.TXO, R1.Pin_0
  N7: U2.RXD, R1.Pin_1, R2.Pin_0
  N8: U2.VCC, U3.OUT+
  N9: U2.GND, U3.OUT-
  VIN: VCC1.+, M1.VIN, Part3.VCC, U3.IN+
  N10: Part2.POS, Part3.POS
  N11: Part2.NEG, Part3.NEG

custom parts:
  ESP8266 ESP-01 Upgraded WiFi Module: Upgraded Version ESP-01,all Flash are upgraded to 1M byte.Also support Cloud service remote transmission.
  HTU21d: Temperature Humidity Sensor, I2C
  FC-28 Soil Hygrometer Module - Probe: The FC-28 is a soil hygrometer module that uses the Texas Instruments LM393 comparator chip to provide an analog measurement of soil humidity.
  FC-28 Soil Hygrometer Module: The FC-28 is a soil hygrometer module that uses the Texas Instruments LM393 comparator chip to provide an analog measurement of soil humidity. The digital output is high when soil moisture is over a certain threshold, as determined by adjusting the potentiometer.
  Mini-360 DC-DC Buck converter: Mini-360 DC-DC Buck converter. Tiny buck step down voltage converter, input voltage 4.75 to 23V output 1 to 17V adjustable. Available from ebay and the like.
  water pump/motor: WATER PUMP BY ARDUBLOCKTR
  IFR520 MOS module: Breakout board for the IFR520 MOSFET transistor. The module is designed to switch heavy DC loads from a single digital pin of your microcontroller. Its main purpose is to provide a low cost way to drive a DC motor for robotics applications, but the module can be used to control most high current DC loads. Screw terminals are provided to interface to your load and external power source. An LED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
